# Fritzing sketch Circuit Fritzing File (saved by Fritzing 0.9.3b)
breadboards: 1

parts:
  Part1 = Arduino Mega ADK (Rev3)
  S1 = H-Bridge with L298N
  M1 = DC Motor
  M2 = DC Motor  # not connected
  J1 = Basic Servo
  VCC1 = 4 x AAA Battery Mount
  Part2 = Bluetooth HC-05 Macho

nets:
  5V: Part1.5V, J1.vcc
  N1: Part1.D11_PWM, S1.IN4
  N2: Part1.D10_PWM, S1.IN3
  GND: Part1.GND, S1.GND, J1.gnd, VCC1.-, Part2.GND
  VIN: Part1.VIN, S1.12V, VCC1.+
  N3: Part1.D0/RX0, Part2.TXD
  N4: Part1.D1/TX0, Part2.RXD
  N5: Part1.D3_PWM, J1.pulse
  N6: Part1.D5_PWM, S1.IN1
  N7: Part1.D6_PWM, S1.IN2
  5V_2: S1.5V, Part2.VCC
  N8: S1.OUT4-Motor2, M1.pin_1

custom parts:
  H-Bridge with L298N: h-bridge
